// Logisim project 1_bit_alu.circ as structural Verilog: 1 circuit, main circuit main
module main (
  input  in_1,
  input  in_2,
  input  in_3,
  input  in_4,
  input  in_5,
  input  in_6,
  input  in_7
);

  wire adder_1_out, and_1_out, multiplexer_1_out, nor_1_out, or_1_out, xor_1_out, xor_2_out;

  xor xor_1 (xor_1_out, in_4, in_1);
  and and_1 (and_1_out, in_3, in_4);
  or or_1 (or_1_out, in_3, in_4);
  xor xor_2 (xor_2_out, in_3, in_4);
  nor nor_1 (nor_1_out, in_3, in_4);
  Adder #(.width(1)) adder_1 (.a(in_3), .b(xor_1_out), .out(adder_1_out), .cin(in_2));  // open: cout
  Multiplexer #(.select(3), .enable("false")) multiplexer_1 (
    .in0(and_1_out), .in1(or_1_out), .in2(xor_2_out), .in3(nor_1_out), .in7(adder_1_out),
    .out(multiplexer_1_out), .sel({in_7, in_6, in_5}));  // open: in4, in5, in6
  LED led_1 (.in(multiplexer_1_out));
endmodule
