// Logisim project ALU_CIRCUITL_224CE8.circ as structural Verilog: 1 circuit, main circuit main
module main (
);

  wire adder_1_cout, adder_1_out, adder_2_cout, adder_2_out, adder_3_cout, adder_3_out, adder_4_cout,
       adder_4_out, multiplexer_1_out, multiplexer_2_out, multiplexer_3_out, multiplexer_4_out, not_1_out,
       not_2_out, not_3_out, not_4_out, not_5_out;
  wire [1:0] counter_1_q;

  not not_1 (not_1_out, 1'b1);
  not not_2 (not_2_out, 1'b1);
  not not_3 (not_3_out, not_1_out);
  not not_4 (not_4_out, 1'b1);
  not not_5 (not_5_out, not_1_out);
  Multiplexer #(.select(2)) multiplexer_1 (
    .in0(1'b1), .in1(not_2_out), .in2(1'b1), .in3(not_1_out), .out(multiplexer_1_out), .sel(counter_1_q),
    .en(1'b1));
  Counter #(.width(2), .max('h3)) counter_1 (.Q(counter_1_q));  // open: load, D, count, carry, clk, clr
  Multiplexer #(.select(2)) multiplexer_2 (
    .in0(not_1_out), .in1(not_3_out), .in2(1'b1), .in3(not_1_out), .out(multiplexer_2_out),
    .sel(counter_1_q), .en(1'b1));
  Multiplexer #(.select(2)) multiplexer_3 (
    .in0(1'b1), .in1(not_4_out), .in2(1'b1), .in3(not_1_out), .out(multiplexer_3_out), .sel(counter_1_q),
    .en(1'b1));
  Multiplexer #(.select(2)) multiplexer_4 (
    .in0(not_1_out), .in1(not_5_out), .in2(1'b1), .in3(not_1_out), .out(multiplexer_4_out),
    .sel(counter_1_q), .en(1'b1));
  Adder #(.width(1)) adder_1 (.a(1'b1), .b(multiplexer_1_out), .out(adder_1_out), .cin(1'b1), .cout(adder_1_cout));
  Adder #(.width(1)) adder_2 (
    .a(not_1_out), .b(multiplexer_2_out), .out(adder_2_out), .cin(adder_1_cout), .cout(adder_2_cout));
  Adder #(.width(1)) adder_3 (
    .a(1'b1), .b(multiplexer_3_out), .out(adder_3_out), .cin(adder_2_cout), .cout(adder_3_cout));
  Adder #(.width(1)) adder_4 (
    .a(not_1_out), .b(multiplexer_4_out), .out(adder_4_out), .cin(adder_3_cout), .cout(adder_4_cout));
  LED led_1 (.in(adder_4_cout));
  LED led_2 (.in(adder_1_out));
  LED led_3 (.in(adder_2_out));
  LED led_4 (.in(adder_3_out));
  LED led_5 (.in(adder_4_out));
  Multiplexer #(.select(2), .enable("false")) multiplexer_5 ();  // open: in0, in1, in2, in3, out, sel
endmodule
